# Fritzing sketch rpizero2w-dht22 (saved by Fritzing 1.0.5)
breadboards: 1

parts:
  RHT1 = Humidity and Temperature Sensor RHT03
  MCU1 = Raspberry Pi Zero
  R1 = Resistor [tolerance=±5% power=0.25W resistance=10k package=THT]

nets:
  N1: RHT1.Vcc, MCU1.pin_1, MCU1.pin_17, R1.Pin_0
  N2: RHT1.Data-signal, MCU1.pin_7
  N3: RHT1.GND_2, MCU1.pin_39, R1.Pin_1
